// Logisim project HW2.circ as structural Verilog: 2 circuits, main circuit main
module main (
);

  // AND_Gate and_1 is placed but not wired
endmodule

module Problem1 (
  input  A,
  input  B,
  input  C,
  input  A_2,
  input  B_2,
  input  C_2,
  output Y,
  output out_8
);

  wire and_1_out, and_2_out, and_3_out, and_4_out, and_5_out, not_1_out, not_2_out;

  and and_1 (and_1_out, A_2, B_2);
  and and_2 (and_2_out, C_2, B_2, not_1_out);
  not not_1 (not_1_out, A_2);
  nor nor_1 (out_8, and_1_out, and_2_out);
  and and_3 (and_3_out, A, B);
  and and_4 (and_4_out, B, C);
  and and_5 (and_5_out, C, B, not_2_out);
  not not_2 (not_2_out, A);
  nor nor_2 (Y, and_3_out, and_4_out, and_5_out);
endmodule
